// Logisim project cpu_32_pipelined.circ as structural Verilog: 6 circuits, main circuit main
module main (
);

  wire clock_1_out, not_1_out, undriven;
  wire [1:0] control_unit_1_ram_write_type;
  wire [2:0] alu_1_eq, control_unit_1_alu_op_type, control_unit_1_imm_type_select,
       control_unit_1_ram_read_type, control_unit_1_write_data_select;
  wire [3:0] register_3_q;
  wire [4:0] DEC_REG_WRITE_ADR_q, EXE_REG_WRITE_ADR_q, WRITE_REG_WRITE_ADR_q;
  wire [9:0] register_2_q;
  wire [14:0] register_1_q;
  wire [14:11] control_unit_1_alu_cmp_type;
  wire [31:0] adder_1_out, adder_2_out, alu_1_alu_result, bit_extender_1_out, DATA_MEMORY_ram_out,
       DEC_ALU_SRC_B_q, DEC_IM_q, DEC_PC4_q, DEC_PC_FINAL_q, DEC_RD1_q, EXE_ALU_RES_q, EXE_IMM_q, EXE_PC4_q,
       EXE_PCIMM_q, EXE_RAM_DATA_IN_q, EXE_SIGN_EXT_q, FETCH_INSTR_q, FETCH_PC4_q, FETCH_PC_q,
       imm_select_1_imm, INSTR_MEMORY_ram_out, multiplexer_1_out, multiplexer_3_out, PC_q, reg_file_1_read_1,
       reg_file_1_read_2, undriven_2, WRITE_ALU_RES_q, WRITE_IMM_q, WRITE_PC4_q, WRITE_PCIMM_q,
       WRITE_SIGN_EXT_q, WRITRE_RAM_OUT_q;

  Clock clock_1 (.out(clock_1_out));
  Adder #(.width(32)) adder_1 (.a(PC_q), .b(32'h4), .out(adder_1_out));  // open: cin, cout
  Multiplexer #(.width(32)) multiplexer_1 (
    .in0(adder_1_out), .in1(adder_2_out), .out(multiplexer_1_out), .sel(register_1_q[14]));
  Register #(.width(32)) PC (.D(multiplexer_1_out), .en(1'b1), .clk(clock_1_out), .Q(PC_q), .clr(undriven));
  Register #(.width(32)) FETCH_INSTR (.D(INSTR_MEMORY_ram_out), .clk(clock_1_out), .Q(FETCH_INSTR_q));  // open: en, clr
  byte_adrr_ram INSTR_MEMORY (
    .READ_CTRL(3'b000), .WRITE_CTRL(2'b11), .WORD_ADDR(PC_q), .RAM_OUT(INSTR_MEMORY_ram_out));  // open: DATA_IN, CLK
  Register #(.width(32)) FETCH_PC (.D(PC_q), .clk(clock_1_out), .Q(FETCH_PC_q));  // open: en, clr
  Register #(.width(32)) FETCH_PC4 (.D(adder_1_out), .clk(clock_1_out), .Q(FETCH_PC4_q));  // open: en, clr
  control_unit control_unit_1 (
    .INSTR(FETCH_INSTR_q), .ALU_FLAGS(alu_1_eq), .WRITE_DATA_SELECT(control_unit_1_write_data_select),
    .RAM_WRITE_TYPE(control_unit_1_ram_write_type), .RAM_READ_TYPE(control_unit_1_ram_read_type),
    .ALU_OP_TYPE(control_unit_1_alu_op_type), .ALU_CMP_TYPE(control_unit_1_alu_cmp_type[11]),
    .ALU_B_OPERAND_SELECT(control_unit_1_alu_cmp_type[12]), .REG_WRITE(control_unit_1_alu_cmp_type[13]),
    .IMM_TYPE_SELECT(control_unit_1_imm_type_select), .PC_SELECT(control_unit_1_alu_cmp_type[14]));
  not not_1 (not_1_out, clock_1_out);
  Register #(.width(15)) register_1 (
    .D({control_unit_1_alu_cmp_type, control_unit_1_alu_op_type, control_unit_1_ram_read_type, control_unit_1_ram_write_type, control_unit_1_write_data_select}),
    .clk(clock_1_out), .Q(register_1_q));  // open: en, clr
  imm_select imm_select_1 (.INSTR(FETCH_INSTR_q), .control(control_unit_1_imm_type_select), .IMM(imm_select_1_imm));
  reg_file reg_file_1 (
    .ADR_2(FETCH_INSTR_q[24:20]), .CLK(not_1_out), .WRITE_ENABLE(register_3_q[3]),
    .WRITE_ADR(WRITE_REG_WRITE_ADR_q), .DATA_IN(multiplexer_3_out), .ADR_1(FETCH_INSTR_q[19:15]),
    .READ_2(reg_file_1_read_2), .READ_1(reg_file_1_read_1));
  Register #(.width(32)) DEC_RD1 (.D(reg_file_1_read_1), .clk(clock_1_out), .Q(DEC_RD1_q));  // open: en, clr
  Register #(.width(32)) DEC_ALU_SRC_B (
    .D(reg_file_1_read_2), .clk(clock_1_out), .Q(DEC_ALU_SRC_B_q));  // open: en, clr
  Register #(.width(32)) DEC_IM (.D(imm_select_1_imm), .clk(clock_1_out), .Q(DEC_IM_q));  // open: en, clr
  Register #(.width(32)) DEC_PC_FINAL (.D(FETCH_PC_q), .clk(clock_1_out), .Q(DEC_PC_FINAL_q));  // open: en, clr
  Register #(.width(5)) DEC_REG_WRITE_ADR (
    .D(FETCH_INSTR_q[11:7]), .clk(clock_1_out), .Q(DEC_REG_WRITE_ADR_q));  // open: en, clr
  Register #(.width(32)) DEC_PC4 (.D(FETCH_PC4_q), .clk(clock_1_out), .Q(DEC_PC4_q));  // open: en, clr
  Multiplexer #(.width(32)) multiplexer_2 (.in0(DEC_ALU_SRC_B_q), .in1(DEC_IM_q), .sel(register_1_q[12]));  // open: out
  Adder #(.width(32)) adder_2 (.a(DEC_IM_q), .b(DEC_PC_FINAL_q), .out(adder_2_out));  // open: cin, cout
  Register #(.width(10)) register_2 (
    .D({1'b0, register_1_q[13], register_1_q[7:0]}), .clk(clock_1_out), .Q(register_2_q));  // open: en, clr
  alu alu_1 (
    .in_2(undriven_2), .in_3(DEC_RD1_q), .ALU_CMPR_CTRL(register_1_q[11]), .ALU_OP_CTRL(register_1_q[10:8]),
    .GT(alu_1_eq[1]), .EQ(alu_1_eq[0]), .LT(alu_1_eq[2]), .ALU_RESULT(alu_1_alu_result));
  assign bit_extender_1_out = {{31{alu_1_eq[2]}}, alu_1_eq[2]};  // Bit_Extender bit_extender_1
  Register #(.width(32)) EXE_SIGN_EXT (.D(bit_extender_1_out), .clk(clock_1_out), .Q(EXE_SIGN_EXT_q));  // open: en, clr
  Register #(.width(32)) EXE_ALU_RES (.D(alu_1_alu_result), .clk(clock_1_out), .Q(EXE_ALU_RES_q));  // open: en, clr
  Register #(.width(32)) EXE_RAM_DATA_IN (.D(undriven_2), .clk(clock_1_out), .Q(EXE_RAM_DATA_IN_q));  // open: en, clr
  Register #(.width(32)) EXE_IMM (.D(DEC_IM_q), .clk(clock_1_out), .Q(EXE_IMM_q));  // open: en, clr
  Register #(.width(32)) EXE_PCIMM (.D(adder_2_out), .clk(clock_1_out), .Q(EXE_PCIMM_q));  // open: en, clr
  Register #(.width(5)) EXE_REG_WRITE_ADR (
    .D(DEC_REG_WRITE_ADR_q), .clk(clock_1_out), .Q(EXE_REG_WRITE_ADR_q));  // open: en, clr
  Register #(.width(32)) EXE_PC4 (.D(DEC_PC4_q), .clk(clock_1_out), .Q(EXE_PC4_q));  // open: en, clr
  Register #(.width(4)) register_3 (
    .D({register_2_q[8], register_2_q[2:0]}), .clk(clock_1_out), .Q(register_3_q));  // open: en, clr
  byte_adrr_ram DATA_MEMORY (
    .READ_CTRL(register_2_q[7:5]), .DATA_IN(EXE_RAM_DATA_IN_q), .WRITE_CTRL(register_2_q[4:3]),
    .WORD_ADDR(EXE_ALU_RES_q), .CLK(clock_1_out), .RAM_OUT(DATA_MEMORY_ram_out));
  Register #(.width(32)) WRITE_SIGN_EXT (.D(EXE_SIGN_EXT_q), .clk(clock_1_out), .Q(WRITE_SIGN_EXT_q));  // open: en, clr
  Register #(.width(32)) WRITRE_RAM_OUT (
    .D(DATA_MEMORY_ram_out), .clk(clock_1_out), .Q(WRITRE_RAM_OUT_q));  // open: en, clr
  Register #(.width(32)) WRITE_ALU_RES (.D(EXE_ALU_RES_q), .clk(clock_1_out), .Q(WRITE_ALU_RES_q));  // open: en, clr
  Register #(.width(32)) WRITE_IMM (.D(EXE_IMM_q), .clk(clock_1_out), .Q(WRITE_IMM_q));  // open: en, clr
  Register #(.width(32)) WRITE_PCIMM (.D(EXE_PCIMM_q), .clk(clock_1_out), .Q(WRITE_PCIMM_q));  // open: en, clr
  Register #(.width(5)) WRITE_REG_WRITE_ADR (
    .D(EXE_REG_WRITE_ADR_q), .clk(clock_1_out), .Q(WRITE_REG_WRITE_ADR_q));  // open: en, clr
  Register #(.width(32)) WRITE_PC4 (.D(EXE_PC4_q), .clk(clock_1_out), .Q(WRITE_PC4_q));  // open: en, clr
  Multiplexer #(.select(3), .width(32)) multiplexer_3 (
    .in2(WRITE_SIGN_EXT_q), .in3(WRITE_ALU_RES_q), .in4(WRITE_IMM_q), .in5(WRITRE_RAM_OUT_q),
    .in6(WRITE_PC4_q), .in7(WRITE_PCIMM_q), .out(multiplexer_3_out), .sel(register_3_q[2:0]));  // open: in0, in1

  // Notes on the sheet:
  //   PC
  //   RD
  //   RS1
  //   RS2
  //   LT
  //   ALU_RESULT
  //   PC+IM
  //   PC+4
  //   IM
endmodule

module alu (
  input  [2:0] ALU_OP_CTRL,
  input  [31:0] in_2,
  input  [31:0] in_3,
  input  ALU_CMPR_CTRL,
  output [31:0] ALU_RESULT,
  output GT,
  output EQ,
  output LT
);

  wire comparator_1_eq, comparator_1_gt, comparator_1_lt, comparator_2_eq, comparator_2_gt, comparator_2_lt;
  wire [4:0] bit_extender_1_out, bit_extender_2_out, bit_extender_3_out;
  wire [31:0] adder_1_out, and_1_out, or_1_out, shifter_1_out, shifter_2_out, shifter_3_out,
       subtractor_1_out, xor_1_out;

  assign or_1_out = in_3 | in_2;  // OR_Gate or_1, 32 bits wide
  assign xor_1_out = in_3 ^ in_2;  // XOR_Gate xor_1, 32 bits wide
  assign and_1_out = in_3 & in_2;  // AND_Gate and_1, 32 bits wide
  Adder #(.width(32)) adder_1 (.a(in_2), .b(in_3), .out(adder_1_out));  // open: cin, cout
  Shifter #(.width(32)) shifter_1 (.in(in_2), .\dist (bit_extender_1_out), .out(shifter_1_out));
  Bit_Extender #(.in_width(32), .out_width(5)) bit_extender_1 (.in(in_3), .out(bit_extender_1_out));
  Shifter #(.shift("lr"), .width(32)) shifter_2 (.in(in_2), .\dist (bit_extender_2_out), .out(shifter_2_out));
  Bit_Extender #(.in_width(32), .out_width(5)) bit_extender_2 (.in(in_3), .out(bit_extender_2_out));
  Shifter #(.shift("ar"), .width(32)) shifter_3 (.in(in_2), .\dist (bit_extender_3_out), .out(shifter_3_out));
  Bit_Extender #(.in_width(32), .out_width(5)) bit_extender_3 (.in(in_3), .out(bit_extender_3_out));
  Subtractor #(.width(32)) subtractor_1 (.a(in_2), .b(in_3), .out(subtractor_1_out));  // open: bin, bout
  Comparator #(.width(32)) comparator_1 (
    .a(in_2), .b(in_3), .gt(comparator_1_gt), .eq(comparator_1_eq), .lt(comparator_1_lt));
  Comparator #(.mode("unsigned"), .width(32)) comparator_2 (
    .a(in_2), .b(in_3), .gt(comparator_2_gt), .eq(comparator_2_eq), .lt(comparator_2_lt));
  Multiplexer multiplexer_1 (.in0(comparator_1_gt), .in1(comparator_2_gt), .out(GT), .sel(ALU_CMPR_CTRL));
  Multiplexer multiplexer_2 (.in0(comparator_1_eq), .in1(comparator_2_eq), .out(EQ), .sel(ALU_CMPR_CTRL));
  Multiplexer multiplexer_3 (.in0(comparator_1_lt), .in1(comparator_2_lt), .out(LT), .sel(ALU_CMPR_CTRL));
  Multiplexer #(.select(3), .width(32)) multiplexer_4 (
    .in0(xor_1_out), .in1(and_1_out), .in2(adder_1_out), .in3(shifter_1_out), .in4(shifter_2_out),
    .in5(shifter_3_out), .in6(subtractor_1_out), .in7(or_1_out), .out(ALU_RESULT), .sel(ALU_OP_CTRL));

  // Notes on the sheet:
  //   A+B
  //   A-B
endmodule

module reg_file (
  input  [4:0] ADR_2,
  input  [4:0] ADR_1,
  input  WRITE_ENABLE,
  input  [4:0] WRITE_ADR,
  input  [31:0] DATA_IN,
  input  CLK,
  output [31:0] READ_1,
  output [31:0] READ_2
);

  wire decoder_1_out1, decoder_1_out2, decoder_1_out3, decoder_1_out4, decoder_1_out5, decoder_1_out6,
       decoder_1_out7, decoder_1_out8, decoder_1_out9, decoder_1_out10, decoder_1_out11, decoder_1_out12,
       decoder_1_out13, decoder_1_out14, decoder_1_out15, decoder_1_out16, decoder_1_out17, decoder_1_out18,
       decoder_1_out19, decoder_1_out20, decoder_1_out21, decoder_1_out22, decoder_1_out23, decoder_1_out24,
       decoder_1_out25, decoder_1_out26, decoder_1_out27, decoder_1_out28, decoder_1_out29, decoder_1_out30,
       decoder_1_out31;
  wire [31:0] undriven, undriven_2, x1_q, x2_q, x3_q, x4_q, x5_q, x6_q, x7_q, x8_q, x9_q, x10_q, x11_q,
       x12_q, x13_q, x14_q, x15_q, x16_q, x17_q, x19_q, x20_q, x21_q, x23_q, x24_q, x25_q, x26_q, x27_q,
       x28_q, x29_q, x30_q, x31_q;

  Decoder #(.select(5)) decoder_1 (
    .out1(decoder_1_out1), .out2(decoder_1_out2), .out3(decoder_1_out3), .out4(decoder_1_out4),
    .out5(decoder_1_out5), .out6(decoder_1_out6), .out7(decoder_1_out7), .out8(decoder_1_out8),
    .out9(decoder_1_out9), .out10(decoder_1_out10), .out11(decoder_1_out11), .out12(decoder_1_out12),
    .out13(decoder_1_out13), .out14(decoder_1_out14), .out15(decoder_1_out15), .out16(decoder_1_out16),
    .out17(decoder_1_out17), .out18(decoder_1_out18), .out19(decoder_1_out19), .out20(decoder_1_out20),
    .out21(decoder_1_out21), .out22(decoder_1_out22), .out23(decoder_1_out23), .out24(decoder_1_out24),
    .out25(decoder_1_out25), .out26(decoder_1_out26), .out27(decoder_1_out27), .out28(decoder_1_out28),
    .out29(decoder_1_out29), .out30(decoder_1_out30), .out31(decoder_1_out31), .sel(WRITE_ADR),
    .en(WRITE_ENABLE));  // open: out0
  Register #(.width(32)) x1 (.D(DATA_IN), .en(decoder_1_out1), .clk(CLK), .Q(x1_q));  // open: clr
  Register #(.width(32)) x2 (.D(DATA_IN), .en(decoder_1_out2), .clk(CLK), .Q(x2_q));  // open: clr
  Register #(.width(32)) x3 (.D(DATA_IN), .en(decoder_1_out3), .clk(CLK), .Q(x3_q));  // open: clr
  Register #(.width(32)) x4 (.D(DATA_IN), .en(decoder_1_out4), .clk(CLK), .Q(x4_q));  // open: clr
  Register #(.width(32)) x5 (.D(DATA_IN), .en(decoder_1_out5), .clk(CLK), .Q(x5_q));  // open: clr
  Register #(.width(32)) x6 (.D(DATA_IN), .en(decoder_1_out6), .clk(CLK), .Q(x6_q));  // open: clr
  Register #(.width(32)) x7 (.D(DATA_IN), .en(decoder_1_out7), .clk(CLK), .Q(x7_q));  // open: clr
  Register #(.width(32)) x8 (.D(DATA_IN), .en(decoder_1_out8), .clk(CLK), .Q(x8_q));  // open: clr
  Register #(.width(32)) x9 (.D(DATA_IN), .en(decoder_1_out9), .clk(CLK), .Q(x9_q));  // open: clr
  Register #(.width(32)) x10 (.D(DATA_IN), .en(decoder_1_out10), .clk(CLK), .Q(x10_q));  // open: clr
  Register #(.width(32)) x11 (.D(DATA_IN), .en(decoder_1_out11), .clk(CLK), .Q(x11_q));  // open: clr
  Register #(.width(32)) x12 (.D(DATA_IN), .en(decoder_1_out12), .clk(CLK), .Q(x12_q));  // open: clr
  Register #(.width(32)) x13 (.D(DATA_IN), .en(decoder_1_out13), .clk(CLK), .Q(x13_q));  // open: clr
  Register #(.width(32)) x14 (.D(DATA_IN), .en(decoder_1_out14), .clk(CLK), .Q(x14_q));  // open: clr
  Register #(.width(32)) x15 (.D(DATA_IN), .en(decoder_1_out15), .clk(CLK), .Q(x15_q));  // open: clr
  Register #(.width(32)) x16 (.D(DATA_IN), .en(decoder_1_out16), .clk(CLK), .Q(x16_q));  // open: clr
  Register #(.width(32)) x17 (.D(DATA_IN), .en(decoder_1_out17), .clk(CLK), .Q(x17_q));  // open: clr
  Register #(.width(32)) x18 (.D(DATA_IN), .en(decoder_1_out18), .clk(CLK));  // open: Q, clr
  Register #(.width(32)) x19 (.D(DATA_IN), .en(decoder_1_out19), .clk(CLK), .Q(x19_q));  // open: clr
  Register #(.width(32)) x20 (.D(DATA_IN), .en(decoder_1_out20), .clk(CLK), .Q(x20_q));  // open: clr
  Register #(.width(32)) x21 (.D(DATA_IN), .en(decoder_1_out21), .clk(CLK), .Q(x21_q));  // open: clr
  Register #(.width(32)) x22 (.D(DATA_IN), .en(decoder_1_out22), .clk(CLK));  // open: Q, clr
  Register #(.width(32)) x23 (.D(DATA_IN), .en(decoder_1_out23), .clk(CLK), .Q(x23_q));  // open: clr
  Register #(.width(32)) x24 (.D(DATA_IN), .en(decoder_1_out24), .clk(CLK), .Q(x24_q));  // open: clr
  Register #(.width(32)) x25 (.D(DATA_IN), .en(decoder_1_out25), .clk(CLK), .Q(x25_q));  // open: clr
  Register #(.width(32)) x26 (.D(DATA_IN), .en(decoder_1_out26), .clk(CLK), .Q(x26_q));  // open: clr
  Register #(.width(32)) x27 (.D(DATA_IN), .en(decoder_1_out27), .clk(CLK), .Q(x27_q));  // open: clr
  Register #(.width(32)) x28 (.D(DATA_IN), .en(decoder_1_out28), .clk(CLK), .Q(x28_q));  // open: clr
  Register #(.width(32)) x29 (.D(DATA_IN), .en(decoder_1_out29), .clk(CLK), .Q(x29_q));  // open: clr
  Register #(.width(32)) x30 (.D(DATA_IN), .en(decoder_1_out30), .clk(CLK), .Q(x30_q));  // open: clr
  Register #(.width(32)) x31 (.D(DATA_IN), .en(decoder_1_out31), .clk(CLK), .Q(x31_q));  // open: clr
  Multiplexer #(.select(5), .width(32)) multiplexer_1 (
    .in0({32{1'b0}}), .in1(x1_q), .in2(x2_q), .in3(x3_q), .in4(x4_q), .in5(x5_q), .in6(x6_q), .in7(x7_q),
    .in8(x8_q), .in9(x9_q), .in10(x10_q), .in11(x11_q), .in12(x12_q), .in13(x13_q), .in14(x14_q),
    .in15(x15_q), .in16(x16_q), .in17(x17_q), .in18(undriven), .in19(x19_q), .in20(x20_q), .in21(x21_q),
    .in22(undriven_2), .in23(x23_q), .in24(x24_q), .in25(x25_q), .in26(x26_q), .in27(x27_q), .in28(x28_q),
    .in29(x29_q), .in30(x30_q), .in31(x31_q), .out(READ_1), .sel(ADR_1));
  Multiplexer #(.select(5), .width(32)) multiplexer_2 (
    .in0({32{1'b0}}), .in1(x1_q), .in2(x2_q), .in3(x3_q), .in4(x4_q), .in5(x5_q), .in6(x6_q), .in7(x7_q),
    .in8(x8_q), .in9(x9_q), .in10(x10_q), .in11(x11_q), .in12(x12_q), .in13(x13_q), .in14(x14_q),
    .in15(x15_q), .in16(x16_q), .in17(x17_q), .in18(undriven), .in19(x19_q), .in20(x20_q), .in21(x21_q),
    .in22(undriven_2), .in23(x23_q), .in24(x24_q), .in25(x25_q), .in26(x26_q), .in27(x27_q), .in28(x28_q),
    .in29(x29_q), .in30(x30_q), .in31(x31_q), .out(READ_2), .sel(ADR_2));
endmodule

module byte_adrr_ram (
  input  [31:0] WORD_ADDR,
  input  [2:0] READ_CTRL,
  input  CLK,
  input  [1:0] WRITE_CTRL,
  input  [31:0] DATA_IN,
  output [31:0] RAM_OUT
);

  wire nand_1_out, nor_1_out, not_1_out;
  wire [7:0] ram_1_dout, ram_2_dout, ram_3_dout, ram_4_dout;
  wire [23:0] adder_1_out, adder_2_out, adder_3_out, bit_extender_1_out;
  wire [31:0] bit_extender_2_out, bit_extender_3_out, bit_extender_4_out, bit_extender_5_out;

  nand nand_1 (nand_1_out, WRITE_CTRL[0], WRITE_CTRL[1]);
  not not_1 (not_1_out, WRITE_CTRL[1]);
  nor nor_1 (nor_1_out, WRITE_CTRL[0], WRITE_CTRL[1]);
  Bit_Extender #(.in_width(32), .out_width(24)) bit_extender_1 (.in(WORD_ADDR), .out(bit_extender_1_out));
  Adder #(.width(24)) adder_1 (.a(bit_extender_1_out), .b(24'h1), .out(adder_1_out));  // open: cin, cout
  Adder #(.width(24)) adder_2 (.a(adder_1_out), .b(24'h1), .out(adder_2_out));  // open: cin, cout
  Adder #(.width(24)) adder_3 (.a(adder_2_out), .b(24'h1), .out(adder_3_out));  // open: cin, cout
  RAM #(.addrWidth(24), .enables("line")) ram_1 (
    .addr(bit_extender_1_out), .we(nand_1_out), .clk(CLK), .din(DATA_IN[7:0]), .dout(ram_1_dout));
  RAM #(.addrWidth(24), .enables("line")) ram_2 (
    .addr(adder_1_out), .we(not_1_out), .clk(CLK), .din(DATA_IN[15:8]), .dout(ram_2_dout));
  RAM #(.addrWidth(24), .enables("line")) ram_3 (
    .addr(adder_2_out), .we(nor_1_out), .clk(CLK), .din(DATA_IN[23:16]), .dout(ram_3_dout));
  RAM #(.addrWidth(24), .enables("line")) ram_4 (
    .addr(adder_3_out), .we(nor_1_out), .clk(CLK), .din(DATA_IN[31:24]), .dout(ram_4_dout));
  assign bit_extender_2_out = {{24{ram_1_dout[7]}}, ram_1_dout};  // Bit_Extender bit_extender_2
  assign bit_extender_3_out = {{24{1'b0}}, ram_1_dout};  // Bit_Extender bit_extender_3
  assign bit_extender_4_out = {{16{ram_2_dout[7]}}, {ram_2_dout, ram_1_dout}};  // Bit_Extender bit_extender_4
  assign bit_extender_5_out = {{16{1'b0}}, {ram_2_dout, ram_1_dout}};  // Bit_Extender bit_extender_5
  Multiplexer #(.select(3), .width(32)) multiplexer_1 (
    .in0({ram_4_dout, ram_3_dout, ram_2_dout, ram_1_dout}), .in2(bit_extender_5_out),
    .in3(bit_extender_4_out), .in4(bit_extender_3_out), .in5(bit_extender_2_out), .out(RAM_OUT),
    .sel(READ_CTRL));  // open: in1, in6, in7
endmodule

module control_unit (
  input  [31:0] INSTR,
  input  [2:0] ALU_FLAGS,
  output [2:0] WRITE_DATA_SELECT,
  output [1:0] RAM_WRITE_TYPE,
  output [2:0] RAM_READ_TYPE,
  output [2:0] ALU_OP_TYPE,
  output ALU_CMP_TYPE,
  output ALU_B_OPERAND_SELECT,
  output REG_WRITE,
  output [2:0] IMM_TYPE_SELECT,
  output PC_SELECT
);

  PLA #(.in_width(20), .out_width(18), .\table ("0000011000xxxxxxxxxx 000011001010111101\n0000011001xxxxxxxxxx 000011001001111101\n0000011010xxxxxxxxxx 000011001000011101\n0000011100xxxxxxxxxx 000011001010011101\n0000011101xxxxxxxxxx 000011001001011101\n0010011000xxxxxxxxxx 000011001000011011\n00100110010000000xxx 000011001100011011\n0010011010xxxxxxxxxx 000011001100011010\n0010011011xxxxxxxxxx 000011101100011010\n0010011100xxxxxxxxxx 000011010100011011\n00100111010000000xxx 000011010000011011\n00100111010100000xxx 000011010100011011\n0010011110xxxxxxxxxx 000011011100011011\n0010011111xxxxxxxxxx 000011000100011011\n0010111xxxxxxxxxxxxx 001010000000011111\n0100011000xxxxxxxxxx 010001001000010000\n0100011001xxxxxxxxxx 010001001000001000\n0100011010xxxxxxxxxx 010001001000000000\n01100110000000000xxx 000010001000011011\n01100110000100000xxx 000010011000011011\n01100110010000000xxx 000010001100011011\n01100110100000000xxx 000010000000011010\n01100110110000000xxx 000010100000011010\n01100111000000000xxx 000010000000011011\n01100111010000000xxx 000010010000011011\n01100111010100000xxx 000010010100011011\n01100111100000000xxx 000010011100011011\n01100111110000000xxx 000010000100011011\n0110111xxxxxxxxxxxxx 001010000000011100\n1100011000xxxxxxxxx1 111100000000011000\n1100011000xxxxxxxxx0 011100000000011000\n1100011001xxxxxxxxx0 111100000000011000\n1100011100xxxxxxx1xx 111100000000011000\n1100011100xxxxxxx0xx 011100000000011000\n1100011101xxxxxxx0x1 111100000000011000\n1100011101xxxxxxx1x0 111100000000011000\n1100011101xxxxxxx1x1 111100000000011000\n1100011101xxxxxxx0x0 011100000000011000\n1100011110xxxxxxx1xx 111100100000011000\n1100011110xxxxxxx0xx 011100100000011000\n1100011111xxxxxxx1x0 111100100000011000\n1100011111xxxxxxx0x1 111100100000011000\n1100011111xxxxxxx1x1 111100100000011000\n1100011111xxxxxxx0x0 011100100000011000\n1100111xxxxxxxxxxxxx 100011001000011110\n1101111xxxxxxxxxxxxx 100111000000011110")) pla_1 (
    .in({INSTR[6:0], INSTR[14:12], INSTR[31:25], ALU_FLAGS}),
    .out({PC_SELECT, IMM_TYPE_SELECT, REG_WRITE, ALU_B_OPERAND_SELECT, ALU_CMP_TYPE, ALU_OP_TYPE, RAM_READ_TYPE, RAM_WRITE_TYPE, WRITE_DATA_SELECT}));

  // Notes on the sheet:
  //   op
  //   func3
  //   func7
endmodule

module imm_select (
  input  [31:0] INSTR,
  input  [2:0] control,
  output [31:0] IMM
);

  wire [31:0] bit_extender_1_out, bit_extender_2_out, bit_extender_3_out, bit_extender_4_out;

  assign bit_extender_1_out = {{11{INSTR[31]}}, {INSTR[31], INSTR[19:12], INSTR[20], INSTR[30:21], 1'b0}};  // Bit_Extender bit_extender_1
  assign bit_extender_2_out = {{20{INSTR[31]}}, INSTR[31:20]};  // Bit_Extender bit_extender_2
  assign bit_extender_3_out = {{20{INSTR[31]}}, {INSTR[31:25], INSTR[11:7]}};  // Bit_Extender bit_extender_3
  assign bit_extender_4_out = {{19{INSTR[31]}}, {INSTR[31], INSTR[7], INSTR[30:25], INSTR[11:8], 1'b0}};  // Bit_Extender bit_extender_4
  Multiplexer #(.select(3), .width(32)) multiplexer_1 (
    .in0(bit_extender_2_out), .in1(bit_extender_1_out), .in2({INSTR[31:12], {12{1'b0}}}),
    .in4(bit_extender_3_out), .in7(bit_extender_4_out), .out(IMM), .sel(control));  // open: in3, in5, in6

  // Notes on the sheet:
  //   I_TYPE_IMMEDIATE
  //   S_TYPE_IMMEDIATE
  //   U_TYPE_IMMEDIATE
  //   J_TYPE_IMMEDIATE
  //   B_TYPE_IMMEDIATE
endmodule
